# Fritzing sketch EsquemaMotor (saved by Fritzing 1.0.5)

parts:
  MCU1 = Raspberry Pi Zero
  J2 = Basic Servo

nets:
  N1: MCU1.pin_2, MCU1.pin_4, J2.vcc
  N2: MCU1.pin_6, MCU1.pin_9, J2.gnd
  N3: MCU1.pin_12, J2.pulse
