# Fritzing sketch EsquemaSensor (saved by Fritzing 1.0.5)

parts:
  U3 = HC-SR04 [chip_label=IC package="SIP (Single Inline) [THT]"]
  MCU1 = Raspberry Pi Zero

nets:
  N1: U3.Vcc, MCU1.pin_2
  N2: U3.Trig, MCU1.pin_16
  N3: U3.Echo, MCU1.pin_18
  N4: U3.GND, MCU1.pin_6, MCU1.pin_9

custom parts:
  HC-SR04: HC-SR04 ultrasound distance sensor
